# Fritzing sketch SmartWaterMeter (saved by Fritzing 0.8.7b)
circuit board: 38.5009cm x 15.4592cm
breadboards: 1

parts:
  Part1 = Arduino Uno (Rev3)
  YF-S201_Flow_Meter2 = YF-S201 Water Flow Meter
  Part2 = Bluetooth HC-05 Macho
  OLED_I2C1 = OLED 128x64 I2C Monochrome Display
  VCC1 = 4 x AAA Battery Mount
  BAT1 = BC9VPC [package=bc9vpc]
  R1 = Resistor [tolerance=±5% resistance=220 package=THT]

nets:
  N1: Part1.A4/SDA, OLED_I2C1.SCK
  N2: Part1.A5/SCL, OLED_I2C1.SDA
  GND: Part1.GND, YF-S201_Flow_Meter2.GND, OLED_I2C1.GND, BAT1.V-
  N3: Part1.D0/RX, Part2.TXD
  N4: Part1.D1/TX, Part2.RXD
  N5: Part1.D2, YF-S201_Flow_Meter2.SIG
  5V: Part1.5V, OLED_I2C1.VDD
  N6: Part1.VIN, R1.Pin_1
  N7: YF-S201_Flow_Meter2.VCC, BAT1.V+, R1.Pin_0
  N8: Part2.VCC, VCC1.+
  N9: Part2.GND, VCC1.-

notes:
  instead of 9v battey an AC to DC power adapter could be used to power arduino. or three seperate 5v sources could be used for all components. or you could power it with your pc using usbA to B.

custom parts:
  YF-S201 Water Flow Meter: The YF-S201 Flow Meter. The input voltage is 5V to 24V (DC).
